// Logisim project new_datapath.circ as structural Verilog: 1 circuit, main circuit main
module main (
  input  [1:0] P1_MOVE,
  input  [1:0] P2_MOVE,
  input  START,
  output [4:0] TOTAL,
  output [1:0] WINNING_PLAYER,
  output P1,
  output D,
  output NUL,
  output P2
);

  wire adder_1_cout, and_1_out, and_2_out, and_3_out, and_4_out, CLK_out, comparator_1_eq, comparator_2_eq,
       comparator_3_eq, comparator_4_eq, comparator_5_eq, comparator_6_eq, comparator_7_eq, comparator_8_eq,
       comparator_9_eq, comparator_10_eq, comparator_11_eq, comparator_12_eq, comparator_13_eq, nor_1_out,
       not_1_out, or_1_out, or_2_out, WIN1_out, WIN2_out;
  wire [1:0] multiplexer_1_out, multiplexer_2_out;
  wire [4:0] adder_1_out, adder_2_out, multiplexer_8_out, multiplexer_9_out, multiplexer_10_out;

  Comparator #(.mode("unsigned"), .width(2)) comparator_1 (
    .a(P1_MOVE), .b(2'b01), .eq(comparator_1_eq));  // open: gt, lt
  Comparator #(.mode("unsigned"), .width(2)) comparator_2 (
    .a(P2_MOVE), .b(2'b11), .eq(comparator_2_eq));  // open: gt, lt
  and and_1 (and_1_out, comparator_1_eq, comparator_2_eq);
  Comparator #(.mode("unsigned"), .width(2)) comparator_3 (
    .a(WINNING_PLAYER), .b(2'b01), .eq(comparator_3_eq));  // open: gt, lt
  Comparator #(.mode("unsigned"), .width(2)) comparator_4 (
    .a(WINNING_PLAYER), .b(2'b11), .eq(comparator_4_eq));  // open: gt, lt
  Comparator #(.mode("unsigned"), .width(2)) comparator_5 (
    .a(WINNING_PLAYER), .b(2'b00), .eq(comparator_5_eq));  // open: gt, lt
  Comparator #(.mode("unsigned"), .width(2)) comparator_6 (
    .a(WINNING_PLAYER), .b(2'b10), .eq(comparator_6_eq));  // open: gt, lt
  nor nor_1 (nor_1_out, comparator_4_eq, comparator_5_eq);
  Comparator #(.mode("unsigned"), .width(2)) comparator_7 (
    .a(P1_MOVE), .b(2'b10), .eq(comparator_7_eq));  // open: gt, lt
  Comparator #(.mode("unsigned"), .width(2)) comparator_8 (
    .a(P2_MOVE), .b(2'b01), .eq(comparator_8_eq));  // open: gt, lt
  and and_2 (and_2_out, comparator_7_eq, comparator_8_eq);
  or or_1 (or_1_out, and_1_out, and_2_out, and_3_out);
  Multiplexer #(.width(2)) multiplexer_1 (.in0(2'b10), .in1(2'b01), .out(multiplexer_1_out), .sel(or_1_out));
  Multiplexer #(.width(2)) multiplexer_2 (
    .in0(multiplexer_1_out), .in1(2'b00), .out(multiplexer_2_out), .sel(or_2_out));
  and WIN1 (WIN1_out, comparator_3_eq, nor_1_out);
  and WIN2 (WIN2_out, nor_1_out, comparator_6_eq);
  Comparator #(.mode("unsigned"), .width(2)) comparator_9 (
    .a(P1_MOVE), .b(2'b11), .eq(comparator_9_eq));  // open: gt, lt
  Multiplexer #(.width(2)) multiplexer_3 (.in0(multiplexer_2_out), .in1(2'b11), .out(WINNING_PLAYER), .sel(and_4_out));
  Multiplexer multiplexer_4 (.in0(WIN1_out), .in1(1'b0), .out(P1), .sel(START));
  Multiplexer multiplexer_5 (.in0(comparator_4_eq), .in1(1'b0), .out(D), .sel(START));
  Multiplexer multiplexer_6 (.in0(comparator_5_eq), .in1(1'b0), .out(NUL), .sel(START));
  Multiplexer multiplexer_7 (.in0(WIN2_out), .in1(1'b0), .out(P2), .sel(START));
  Comparator #(.mode("unsigned"), .width(2)) comparator_10 (
    .a(P2_MOVE), .b(2'b10), .eq(comparator_10_eq));  // open: gt, lt
  and and_3 (and_3_out, comparator_9_eq, comparator_10_eq);
  Comparator #(.mode("unsigned"), .width(2)) comparator_11 (
    .a(P1_MOVE), .b(2'b00), .eq(comparator_11_eq));  // open: gt, lt
  Comparator #(.mode("unsigned"), .width(2)) comparator_12 (
    .a(P2_MOVE), .b(2'b00), .eq(comparator_12_eq));  // open: gt, lt
  or or_2 (or_2_out, comparator_11_eq, comparator_12_eq);
  not not_1 (not_1_out, or_2_out);
  and and_4 (and_4_out, not_1_out, comparator_13_eq);
  Clock CLK (.out(CLK_out));
  Comparator #(.mode("unsigned"), .width(2)) comparator_13 (
    .a(P2_MOVE), .b(P1_MOVE), .eq(comparator_13_eq));  // open: gt, lt
  Multiplexer #(.select(2), .width(5)) multiplexer_8 (
    .in0({5{1'b0}}), .in1(5'b00100), .in2(5'b01000), .in3(5'b01100), .out(multiplexer_8_out), .sel(P1_MOVE));
  Multiplexer #(.select(2), .width(5)) multiplexer_9 (
    .in0({5{1'b0}}), .in1(5'b00001), .in2(5'b00010), .in3(5'b00011), .out(multiplexer_9_out), .sel(P2_MOVE));
  Adder #(.width(5)) adder_1 (
    .a(multiplexer_9_out), .b(multiplexer_8_out), .out(adder_1_out), .cout(adder_1_cout));  // open: cin
  Adder #(.width(5)) adder_2 (.a(adder_1_out), .b(5'b00100), .out(adder_2_out));  // open: cin, cout
  Multiplexer #(.width(5)) multiplexer_10 (.in0(TOTAL), .in1(adder_2_out), .out(multiplexer_10_out), .sel(START));
  Register #(.width(5)) FINAL_MANCHE (.D(multiplexer_10_out), .Q(TOTAL), .clk(CLK_out));  // open: en, clr

  // Notes on the sheet:
  //   MANCHE WINNER LOGIC
  //   CONTROL SIGNALS
  //   SET TOTAL MANCHE
endmodule
